// Logisim project 8051.circ as structural Verilog
module ALU (
  input  CarryFlagPin,
  input  CarryIn,
  input  [7:0] Accumulator,
  input  [7:0] RegisterB,
  input  [2:0] Opcode,
  output CarryFlag,
  output [7:0] out_7
);

  wire multiplexer_1_out;
  wire [7:0] adder_1_out, adder_2_out, divider_1_out, divider_1_rem, multiplexer_2_out, multiplier_1_out,
       negator_1_out;

  Multiplexer #(.select(3)) multiplexer_1 (
    .in0(1'b0), .in1(1'b0), .in2(1'b0), .in3(CarryIn), .out(multiplexer_1_out), .sel(Opcode));  // open: in4, in5, in6, in7
  Multiplexer #(.select(3), .width(8)) multiplexer_2 (
    .in0(8'h1), .in1({8{1'b1}}), .in2(RegisterB), .in3(RegisterB), .in4(negator_1_out),
    .out(multiplexer_2_out), .sel(Opcode));  // open: in5, in6, in7
  // OR_Gate or_1 has open pins: in0=RegisterB, in1=Accumulator, out=open
  Adder adder_1 (.a({8{1'b0}}), .b(RegisterB), .out(adder_1_out), .cin(CarryIn));  // open: cout
  Adder adder_2 (.a(Accumulator), .b(multiplexer_2_out), .out(adder_2_out), .cin(multiplexer_1_out), .cout(CarryFlag));
  Negator negator_1 (.in(adder_1_out), .out(negator_1_out));
  // Buffer buffer_1 has open pins: in=CarryFlagPin, out=open
  Multiplier multiplier_1 (.a(RegisterB), .b(Accumulator), .out(multiplier_1_out));  // open: cin, cout
  Divider divider_1 (.a(Accumulator), .b(RegisterB), .out(divider_1_out), .rem(divider_1_rem));  // open: upper
  assign out_7 = adder_2_out | multiplier_1_out | divider_1_out;  // OR_Gate or_2, 8 bits wide

  // Notes on the sheet:
  //   -1
  //   in case of DIV, it goes to register B
endmodule

module ALU_v2 (
  input  Carry,
  input  [7:0] Buffer1,
  input  [7:0] Buffer2,
  input  [2:0] in_4,
  output [7:0] out_5
);

  wire [7:0] adder_1_out, adder_2_out, adder_3_out, adder_4_out, adder_5_out, adder_6_out, divider_1_out,
       divider_1_rem, multiplexer_1_out, multiplier_1_out, negator_1_out;
  wire [15:0] bit_extender_1_out, bit_extender_2_out;

  Adder adder_1 (.a({8{1'b0}}), .b(Buffer2), .out(adder_1_out), .cin(Carry));  // open: cout
  Negator negator_1 (.in(adder_1_out), .out(negator_1_out));
  assign bit_extender_1_out = {{8{Buffer2[7]}}, Buffer2};  // Bit_Extender bit_extender_1
  assign bit_extender_2_out = {{8{Buffer1[7]}}, Buffer1};  // Bit_Extender bit_extender_2
  Adder adder_2 (.a(8'h1), .b(Buffer1), .out(adder_2_out));  // open: cin, cout
  Adder adder_3 (.a({8{1'b1}}), .b(Buffer1), .out(adder_3_out));  // open: cin, cout
  Adder adder_4 (.a(Buffer1), .b(Buffer2), .out(adder_4_out));  // open: cin, cout
  Adder adder_5 (.a(Buffer1), .b(Buffer2), .out(adder_5_out), .cin(Carry));  // open: cout
  Adder adder_6 (.a(Buffer1), .b(negator_1_out), .out(adder_6_out));  // open: cin, cout
  Multiplier #(.width(16)) multiplier_1 (
    .a(bit_extender_1_out), .b(bit_extender_2_out), .out({out_5, multiplier_1_out}));  // open: cin, cout
  Divider divider_1 (.out(divider_1_out), .rem(divider_1_rem));  // open: a, b, upper
  // Probe on multiplexer_1_out
  Multiplexer #(.select(3), .width(8)) multiplexer_1 (
    .in0(adder_2_out), .in1(adder_3_out), .in2(adder_4_out), .in3(adder_5_out), .in4(adder_6_out),
    .in5(multiplier_1_out), .in6(divider_1_out), .out(multiplexer_1_out), .sel(in_4));  // open: in7
  Multiplexer #(.select(3), .width(8)) multiplexer_2 ();  // open: in0, in1, in2, in3, in4, in5, in6, in7, out, sel

  // Notes on the sheet:
  //   ALU ->
  //   ->
  //   to register B
endmodule
